// Logisim project TP3_EX1_XNOR.circ as structural Verilog: 1 circuit, main circuit main
module main (
  input  in_1,
  input  in_2,
  input  in_3,
  input  in_4,
  input  in_5,
  input  [3:0] in_6,
  input  in_7,
  output [3:0] out_8
);

  // XNOR_Gate xnor_1 has open pins: in0=in_5, in1=in_1, out=open
  xnor xnor_2 (out_8[3], in_7, in_6[0]);
  // XNOR_Gate xnor_3 has open pins: in0=in_5, in1=in_2, out=open
  xnor xnor_4 (out_8[2], in_7, in_6[1]);
  // XNOR_Gate xnor_5 has open pins: in0=in_5, in1=in_3, out=open
  xnor xnor_6 (out_8[1], in_7, in_6[2]);
  // XNOR_Gate xnor_7 has open pins: in0=in_5, in1=in_4, out=open
  xnor xnor_8 (out_8[0], in_7, in_6[3]);
endmodule
