// Logisim project TP3_EX4_ALU_pas_fini.circ as structural Verilog: 1 circuit, main circuit main
module main (
  input  [1:0] A,
  input  [1:0] B,
  input  in_3,
  input  in_4,
  input  [7:0] in_5,
  input  in_6,
  output out_7,
  output out_8,
  output A_B,
  output [1:0] A_B_2,
  output [1:0] A_B_3,
  output [1:0] A_B_4,
  output [1:0] A_B_5,
  output A_B_6,
  output out_15,
  output [1:0] A_B_7
);

  wire and_1_out, and_2_out, and_3_out, and_4_out, and_5_out, and_6_out, and_7_out, and_8_out, and_9_out,
       and_10_out, and_11_out, and_12_out, and_13_out, and_14_out, and_15_out, and_16_out, and_17_out,
       not_1_out, not_2_out, not_3_out, not_4_out, not_5_out, not_6_out, not_7_out, or_3_out, or_4_out,
       or_6_out, xnor_1_out, xor_1_out, xor_3_out, xor_5_out, xor_7_out, xor_9_out, xor_11_out;

  or or_1 (out_7, and_1_out, and_2_out);
  and and_1 (and_1_out, A[1], B[1]);
  and and_2 (and_2_out, xor_1_out, or_3_out);
  or or_2 (out_15, and_4_out, and_5_out);
  xor xor_1 (xor_1_out, A[1], B[1]);
  xor xor_2 (A_B_2[1], xor_1_out, or_3_out);
  not not_1 (not_1_out, in_5[1]);
  and and_3 (and_3_out, not_1_out, in_5[0]);
  and and_4 (and_4_out, in_5[4], in_5[6]);
  and and_5 (and_5_out, xor_3_out, or_4_out);
  and and_6 (and_6_out, A[0], B[0]);
  or or_3 (or_3_out, and_6_out, and_7_out);
  and and_7 (and_7_out, xor_5_out, in_3);
  xor xor_3 (xor_3_out, in_5[4], in_5[6]);
  xor xor_4 (A_B_7[0], xor_3_out, or_4_out);
  and and_8 (and_8_out, in_5[5], in_5[7]);
  or or_4 (or_4_out, and_8_out, and_9_out);
  and and_9 (and_9_out, xor_7_out, in_6);
  xor xor_5 (xor_5_out, A[0], B[0]);
  xor xor_6 (A_B_2[0], xor_5_out, in_3);
  xor xor_7 (xor_7_out, in_5[5], in_5[7]);
  xor xor_8 (A_B_7[1], xor_7_out, in_6);
  or or_5 (out_8, and_11_out, and_12_out);
  not not_2 (not_2_out, in_5[0]);
  not not_3 (not_3_out, in_5[1]);
  and and_10 (and_10_out, not_3_out, not_2_out);
  and and_11 (and_11_out, A[1], not_4_out);
  and and_12 (and_12_out, xor_9_out, or_6_out);
  not not_4 (not_4_out, B[1]);
  or or_6 (or_6_out, and_13_out, and_14_out);
  xor xor_9 (xor_9_out, A[1], not_4_out);
  xor xor_10 (A_B_3[1], xor_9_out, or_6_out);
  and and_13 (and_13_out, A[0], not_5_out);
  and and_14 (and_14_out, xor_11_out, in_4);
  not not_5 (not_5_out, B[0]);
  xor xor_11 (xor_11_out, A[0], not_5_out);
  xor xor_12 (A_B_3[0], xor_11_out, in_4);
  not not_6 (not_6_out, A[1]);
  and and_15 (and_15_out, not_6_out, B[1]);
  or or_7 (A_B, and_15_out, and_17_out);
  not not_7 (not_7_out, A[0]);
  and and_16 (and_16_out, not_7_out, B[0]);
  xnor xnor_1 (xnor_1_out, A[1], B[1]);
  and and_17 (and_17_out, xnor_1_out, and_16_out);

  assign A_B_4 = A_B_2;
  assign A_B_5 = A_B_3;
  assign A_B_6 = A_B;

  // Notes on the sheet:
  //   RESULTAT:
  //   lth
  //   add
  //   A
  //   B
  //   minus
  //   choix op
endmodule
