// Logisim project exo3a.circ as structural Verilog: 1 circuit, main circuit main
module main (
  input  a,
  input  b,
  input  c,
  output s
);

  wire and_1_out;

  and and_1 (and_1_out, a, b);
  or or_1 (s, c, and_1_out);
endmodule
