// Logisim project exercice1.circ as structural Verilog: 1 circuit, main circuit main
module main (
  input  [3:0] in_1,
  input  in_2,
  output [3:0] out_3
);

  xor xor_1 (out_3[3], ~in_1[3], in_2);  // XOR_Gate
  xor xor_2 (out_3[2], ~in_1[2], in_2);  // XOR_Gate
  xor xor_3 (out_3[2], ~in_1[2], in_2);  // XOR_Gate
  xor xor_4 (out_3[1], ~in_1[1], in_2);  // XOR_Gate
  xor xor_5 (out_3[0], ~in_1[0], in_2);  // XOR_Gate
endmodule
