// Logisim project exercice3.circ as structural Verilog: 1 circuit, main circuit main
module main (
  input  [3:0] A,
  input  [3:0] B,
  input  [3:0] C,
  input  [3:0] D,
  input  [1:0] R0,
  input  [1:0] R1,
  output out_7
);

  wire and_1_out, and_2_out, and_3_out, and_4_out, and_5_out, and_6_out, and_7_out, or_2_out, or_3_out,
       xnor_1_out, xnor_2_out, xnor_3_out;
  wire [3:0] multiplexer_1_out, multiplexer_2_out;

  Multiplexer #(.select(2), .width(4), .enable("false")) multiplexer_1 (
    .in0(A), .in1(B), .in2(C), .in3(D), .out(multiplexer_1_out), .sel(R1));
  Multiplexer #(.select(2), .width(4), .enable("false")) multiplexer_2 (
    .in0(A), .in1(B), .in2(C), .in3(D), .out(multiplexer_2_out), .sel(R0));
  and and_1 (and_1_out, ~multiplexer_2_out[3], multiplexer_1_out[3]);  // AND_Gate
  or or_1 (out_7, and_1_out, and_2_out);
  xnor xnor_1 (xnor_1_out, multiplexer_2_out[3], multiplexer_1_out[3]);
  and and_2 (and_2_out, xnor_1_out, or_2_out);
  and and_3 (and_3_out, ~multiplexer_2_out[2], multiplexer_1_out[2]);  // AND_Gate
  xnor xnor_2 (xnor_2_out, multiplexer_2_out[2], multiplexer_1_out[2]);
  and and_4 (and_4_out, xnor_2_out, or_3_out);
  or or_2 (or_2_out, and_3_out, and_4_out);
  and and_5 (and_5_out, ~multiplexer_2_out[1], multiplexer_1_out[1]);  // AND_Gate
  or or_3 (or_3_out, and_5_out, and_6_out);
  xnor xnor_3 (xnor_3_out, multiplexer_2_out[1], multiplexer_1_out[1]);
  and and_6 (and_6_out, xnor_3_out, and_7_out);
  and and_7 (and_7_out, ~multiplexer_2_out[0], multiplexer_1_out[0]);  // AND_Gate
endmodule
