// Logisim project tp_1.circ as structural Verilog: 10 circuits, main circuit main
module main (
  input  in_1
);

  // AND_Gate and_1 has open pins: in0=in_1, out=open
  // OR_Gate or_1 is placed but not wired
endmodule

module portenot (
  input  in_1,
  output out_2
);

  Pull_Resistor #(.pull(1)) pull_resistor_1 (.node(out_2));
  Transistor #(.\type ("n")) transistor_1 (.in(1'b0), .out(out_2), .gate(in_1));
endmodule

module porteNOR (
  input  in_1,
  input  in_2,
  output out_3
);

  Pull_Resistor #(.pull(1)) pull_resistor_1 (.node(out_3));
  Transistor #(.\type ("n")) transistor_1 (.in(1'b0), .out(out_3), .gate(in_1));
  Transistor #(.\type ("n")) transistor_2 (.in(1'b0), .out(out_3), .gate(in_2));
endmodule

module porteNAND (
  input  in_1,
  input  in_2,
  output out_3
);

  wire transistor_2_out;

  Pull_Resistor #(.pull(1)) pull_resistor_1 (.node(out_3));
  Transistor #(.\type ("n")) transistor_1 (.in(transistor_2_out), .out(out_3), .gate(in_1));
  Transistor #(.\type ("n")) transistor_2 (.in(1'b0), .out(transistor_2_out), .gate(in_2));
endmodule

module porteXOR (
  input  za,
  input  zb,
  input  a,
  input  b,
  output out_5
);

  wire and_1_out, and_2_out, not_1_out, not_2_out, not_3_out, not_4_out, or_1_out, transistor_1_out,
       transistor_2_out, transistor_3_out, transistor_4_out, transistor_5_out, transistor_6_out,
       transistor_7_out, transistor_8_out, undriven;

  not not_1 (not_1_out, transistor_1_out);
  Transistor #(.\type ("n")) transistor_1 (.in(1'b0), .out(transistor_1_out), .gate(za));
  Transistor #(.\type ("n")) transistor_2 (.in(1'b0), .out(transistor_2_out), .gate(zb));
  not not_2 (not_2_out, zb);
  Transistor #(.\type ("n")) transistor_3 (.in(1'b0), .out(transistor_3_out), .gate(a));
  Transistor #(.\type ("n")) transistor_4 (.in(1'b0), .out(transistor_4_out), .gate(b));
  and and_1 (and_1_out, not_1_out, transistor_2_out);
  and and_2 (and_2_out, za, not_2_out);
  Transistor #(.\type ("n")) transistor_5 (.in(1'b0), .out(transistor_5_out), .gate(transistor_3_out));
  Transistor #(.\type ("n")) transistor_6 (.in(b), .out(transistor_6_out), .gate(b));
  not not_3 (not_3_out, and_1_out);
  not not_4 (not_4_out, and_2_out);
  Transistor #(.\type ("n")) transistor_7 (.in(undriven), .out(transistor_7_out), .gate(transistor_5_out));
  Transistor #(.\type ("n")) transistor_8 (.in(1'b0), .out(transistor_8_out), .gate(transistor_7_out));
  Transistor #(.\type ("n")) transistor_9 (.in(undriven), .out(transistor_7_out), .gate(transistor_4_out));
  or or_1 (or_1_out, not_3_out, not_4_out);
  not not_5 (out_5, or_1_out);
  Pull_Resistor #(.pull(1)) pull_resistor_1 (.node(out_5));
  // also tied to GND on the sheet: {a, b}

  // Notes on the sheet:
  //   a
  //   b
  //   a
  //   b
endmodule

module NmosNOT (
  input  in_1,
  output out_2
);

  Transistor transistor_1 (.in(1'b1), .out(out_2), .gate(in_1));
  Pull_Resistor pull_resistor_1 (.node(out_2));
endmodule

module cmosex5 (
  input  a,
  input  b,
  input  d,
  input  c,
  input  in_5,
  input  in_6,
  output out_7
);

  wire pull_resistor_1_node, pull_resistor_2_node, transistor_2_out;

  Pull_Resistor #(.pull(1)) pull_resistor_1 (.node(pull_resistor_1_node));
  // Probe on pull_resistor_1_node
  Transistor #(.\type ("n"), .gate("br")) transistor_1 (.in(transistor_2_out), .out(pull_resistor_1_node), .gate(b));
  Transistor #(.\type ("n")) transistor_2 (.in(1'b0), .out(transistor_2_out), .gate(a));
  Transistor #(.\type ("n")) transistor_3 (.gate(in_5));  // open: in, out
  // Probe on nothing
  Pull_Resistor #(.pull(1)) pull_resistor_2 (.node(pull_resistor_2_node));
  Transistor #(.\type ("n")) transistor_4 (.in(1'b0), .out(pull_resistor_2_node), .gate(pull_resistor_1_node));
  Transistor #(.\type ("n"), .gate("br")) transistor_5 (.in(1'b0), .out(pull_resistor_2_node), .gate(c));
  Pull_Resistor #(.pull(1)) pull_resistor_3 (.node(pull_resistor_2_node));
  Pull_Resistor #(.pull(1)) pull_resistor_4 (.node(pull_resistor_2_node));
  Transistor #(.\type ("n"), .gate("br")) transistor_6 (.in(1'b0), .out(pull_resistor_2_node), .gate(d));
  Transistor #(.\type ("n")) transistor_7 (.in(1'b0), .out(out_7), .gate(pull_resistor_2_node));
  Pull_Resistor #(.pull(1)) pull_resistor_5 (.node(out_7));

  // Notes on the sheet:
  //   pb avec le a.b
endmodule

module exo5 (
  input  a,
  input  b,
  input  c,
  input  d,
  input  a_2,
  input  b_2,
  input  c_2,
  input  d_2,
  output a_b_c_d,
  output a_b_c_d_2,
  output out_11,
  output out_12,
  output out_13,
  output out_14,
  output out_15
);

  wire and_1_out, or_1_out, transistor_1_out, transistor_10_out, transistor_11_out, transistor_18_out;

  Transistor #(.\type ("n")) transistor_1 (.in(1'b0), .out(transistor_1_out), .gate(a_2));
  Transistor #(.\type ("n")) transistor_2 (.in(1'b0), .out(out_14), .gate(c_2));
  Transistor #(.\type ("n"), .gate("br")) transistor_3 (.in(1'b0), .out(out_14), .gate(d_2));
  and and_1 (and_1_out, a, b);
  or or_1 (or_1_out, c, d);
  Transistor transistor_4 (.in(1'b1), .out(out_11), .gate(b_2));
  Transistor #(.\type ("n")) transistor_5 (.in(transistor_1_out), .out(out_11), .gate(b_2));
  Transistor #(.gate("br")) transistor_6 (.in(1'b1), .out(out_11), .gate(a_2));
  Transistor #(.\type ("n")) transistor_7 (.in(1'b0), .out(out_13), .gate(out_11));
  Transistor transistor_8 (.in(1'b1), .out(out_13), .gate(out_11));
  Transistor transistor_9 (.in(transistor_10_out), .out(out_14), .gate(c_2));
  Transistor transistor_10 (.in(1'b1), .out(transistor_10_out), .gate(d_2));
  or or_2 (a_b_c_d, and_1_out, or_1_out);
  Transistor #(.\type ("n")) transistor_11 (.in(1'b0), .out(transistor_11_out), .gate(out_13));
  Transistor transistor_12 (.in(transistor_18_out), .out(transistor_11_out), .gate(out_13));
  Transistor #(.\type ("n"), .gate("br")) transistor_13 (.in(1'b0), .out(transistor_11_out), .gate(out_15));
  Transistor #(.\type ("n")) transistor_14 (.in(1'b0), .out(out_15), .gate(out_14));
  Transistor transistor_15 (.in(1'b1), .out(out_15), .gate(out_14));
  Transistor transistor_16 (.in(1'b1), .out(a_b_c_d_2), .gate(transistor_11_out));
  Transistor #(.\type ("n")) transistor_17 (.in(1'b0), .out(a_b_c_d_2), .gate(transistor_11_out));
  Transistor transistor_18 (.in(1'b1), .out(transistor_18_out), .gate(out_15));

  assign out_12 = 1'b1;

  // Notes on the sheet:
  //   a.b
  //   a.b
  //   c+d
endmodule

module exo6 (
  input  in_1,
  input  in_2,
  input  a,
  input  b,
  output out_5,
  output nor_a_b,
  output out_7,
  output out_8,
  output out_9,
  output XOR,
  output out_11
);

  wire and_1_out, not_1_out, or_1_out, transistor_3_out, transistor_5_out, transistor_13_out;

  Transistor #(.\type ("n")) transistor_1 (.in(1'b0), .out(nor_a_b), .gate(a));
  Transistor #(.\type ("n"), .gate("br")) transistor_2 (.in(1'b0), .out(nor_a_b), .gate(b));
  Transistor #(.\type ("n")) transistor_3 (.in(1'b0), .out(transistor_3_out), .gate(a));
  or or_1 (or_1_out, in_1, in_2);
  and and_1 (and_1_out, in_1, in_2);
  Transistor transistor_4 (.in(transistor_5_out), .out(nor_a_b), .gate(a));
  Transistor transistor_5 (.in(1'b1), .out(transistor_5_out), .gate(b));
  Transistor transistor_6 (.in(1'b1), .out(out_8), .gate(b));
  Transistor #(.\type ("n")) transistor_7 (.in(transistor_3_out), .out(out_8), .gate(b));
  Transistor #(.gate("br")) transistor_8 (.in(1'b1), .out(out_8), .gate(a));
  Transistor #(.\type ("n")) transistor_9 (.in(1'b0), .out(out_11), .gate(out_8));
  not not_1 (not_1_out, or_1_out);
  Transistor transistor_10 (.in(1'b1), .out(out_11), .gate(out_8));
  or or_2 (out_5, not_1_out, and_1_out);
  Transistor #(.\type ("n")) transistor_11 (.in(1'b0), .out(out_7), .gate(nor_a_b));
  Transistor transistor_12 (.in(transistor_13_out), .out(out_7), .gate(nor_a_b));
  Transistor transistor_13 (.in(1'b1), .out(transistor_13_out), .gate(out_11));
  Transistor #(.\type ("n"), .gate("br")) transistor_14 (.in(1'b0), .out(out_7), .gate(out_11));
  Transistor transistor_15 (.in(1'b1), .out(XOR), .gate(out_7));
  Transistor #(.\type ("n")) transistor_16 (.in(1'b0), .out(XOR), .gate(out_7));

  assign out_9 = 1'b1;

  // Notes on the sheet:
  //   a
  //   b
  //   not( nand(a.b) )
endmodule

module exo7 (
  input  a,
  input  S,
  input  b,
  output out_4
);

  wire transistor_1_out;

  Transistor transistor_1 (.in(1'b1), .out(transistor_1_out), .gate(S));
  Transistor #(.\type ("n")) transistor_2 (.in(1'b0), .out(transistor_1_out), .gate(S));
  Transistor transistor_3 (.in(a), .out(out_4), .gate(S));
  Transistor #(.\type ("n"), .gate("br")) transistor_4 (.in(a), .out(out_4), .gate(transistor_1_out));
  Transistor transistor_5 (.in(b), .out(out_4), .gate(transistor_1_out));
  Transistor #(.\type ("n"), .gate("br")) transistor_6 (.in(b), .out(out_4), .gate(S));
endmodule
