// Logisim project TP3_EX2_A_moins_B_4bits.circ as structural Verilog: 1 circuit, main circuit main
module main (
  input  Rin,
  input  in_2,
  input  in_3,
  input  [1:0] in_4,
  input  [1:0] in_5,
  input  in_6,
  input  [3:0] in_7,
  input  [3:0] in_8,
  input  On_ajoute_1,
  output [1:0] out_10,
  output out_11,
  output out_12,
  output [3:0] out_13
);

  wire adder_1_cout, and_1_out, and_2_out, and_3_out, and_4_out, and_5_out, and_6_out, and_7_out, and_8_out,
       and_9_out, and_10_out, not_1_out, not_2_out, not_3_out, not_4_out, or_2_out, or_3_out, or_4_out,
       or_5_out, xor_1_out, xor_2_out, xor_4_out, xor_5_out, xor_7_out, xor_9_out;

  or or_1 (out_12, and_1_out, and_2_out);
  and and_1 (and_1_out, in_7[3], not_1_out);
  and and_2 (and_2_out, xor_2_out, or_3_out);
  and and_3 (and_3_out, in_2, in_3);
  or or_2 (or_2_out, and_3_out, and_4_out);
  xor xor_1 (xor_1_out, in_2, in_3);
  Adder #(.width(1)) adder_1 (.a(in_4[0]), .b(in_5[0]), .out(out_10[0]), .cin(in_6), .cout(adder_1_cout));
  Adder #(.width(1)) adder_2 (.a(in_5[1]), .b(in_4[1]), .out(out_10[1]), .cin(adder_1_cout), .cout(out_11));
  not not_1 (not_1_out, in_8[3]);
  xor xor_2 (xor_2_out, in_7[3], not_1_out);
  xor xor_3 (out_13[3], xor_2_out, or_3_out);
  and and_4 (and_4_out, xor_1_out, Rin);
  or or_3 (or_3_out, and_5_out, and_6_out);
  xor xor_4 (xor_4_out, xor_1_out, Rin);
  and and_5 (and_5_out, in_7[2], not_2_out);
  and and_6 (and_6_out, xor_5_out, or_4_out);
  not not_2 (not_2_out, in_8[2]);
  xor xor_5 (xor_5_out, in_7[2], not_2_out);
  xor xor_6 (out_13[2], xor_5_out, or_4_out);
  or or_4 (or_4_out, and_7_out, and_8_out);
  and and_7 (and_7_out, in_7[1], not_3_out);
  and and_8 (and_8_out, xor_7_out, or_5_out);
  xor xor_7 (xor_7_out, in_7[1], not_3_out);
  not not_3 (not_3_out, in_8[1]);
  xor xor_8 (out_13[1], xor_7_out, or_5_out);
  or or_5 (or_5_out, and_9_out, and_10_out);
  and and_9 (and_9_out, in_7[0], not_4_out);
  and and_10 (and_10_out, xor_9_out, On_ajoute_1);
  xor xor_9 (xor_9_out, in_7[0], not_4_out);
  not not_4 (not_4_out, in_8[0]);
  xor xor_10 (out_13[0], xor_9_out, On_ajoute_1);

  // Notes on the sheet:
  //   a
  //   B
  //   Retire le 1 de Gauche
  //   S A-B
  //   A
  //   b
  //   Rout
  //   Rout
  //   Rin
  //   s
  //   On inverse B
endmodule
