// Logisim project TP3_EX3_A_inferieur_B_4bits.circ as structural Verilog: 1 circuit, main circuit main
module main (
  input  [3:0] A,
  input  [3:0] B,
  input  [3:0] A_2,
  input  [3:0] B_2,
  output A_B,
  output A_B_2
);

  wire and_1_out, and_2_out, and_3_out, and_4_out, and_5_out, and_6_out, and_7_out, not_1_out, not_2_out,
       not_3_out, not_4_out, xnor_1_out, xnor_2_out, xnor_3_out, xnor_4_out, xnor_5_out, xnor_6_out;

  not not_1 (not_1_out, A[3]);
  and and_1 (and_1_out, not_1_out, B[3]);
  xnor xnor_1 (xnor_1_out, A[3], B[3]);
  and and_2 (and_2_out, xnor_1_out, and_3_out);
  Comparator #(.width(4)) comparator_1 (.a(A_2), .b(B_2), .lt(A_B_2));  // open: gt, eq
  not not_2 (not_2_out, A[2]);
  and and_3 (and_3_out, not_2_out, B[2]);
  xnor xnor_2 (xnor_2_out, A[3], B[3]);
  xnor xnor_3 (xnor_3_out, A[2], B[2]);
  and and_4 (and_4_out, xnor_2_out, xnor_3_out, and_5_out);
  or or_1 (A_B, and_1_out, and_2_out, and_4_out, and_6_out);
  not not_3 (not_3_out, A[1]);
  and and_5 (and_5_out, not_3_out, B[1]);
  xnor xnor_4 (xnor_4_out, A[3], B[3]);
  xnor xnor_5 (xnor_5_out, A[2], B[2]);
  xnor xnor_6 (xnor_6_out, A[1], B[2]);
  and and_6 (and_6_out, xnor_4_out, xnor_5_out, xnor_6_out, and_7_out);
  not not_4 (not_4_out, A[0]);
  and and_7 (and_7_out, not_4_out, B[0]);
endmodule
