// Logisim project TP3_EX3_A_plus_B_4bits.circ as structural Verilog: 1 circuit, main circuit main
module main (
  input  [3:0] A,
  input  [3:0] B,
  input  in_3,
  output out_4,
  output [3:0] out_5
);

  wire and_1_out, and_2_out, and_3_out, and_4_out, and_5_out, and_6_out, and_7_out, and_8_out, or_2_out,
       or_3_out, or_4_out, xor_1_out, xor_3_out, xor_5_out, xor_7_out;

  or or_1 (out_4, and_1_out, and_2_out);
  and and_1 (and_1_out, A[3], B[3]);
  and and_2 (and_2_out, xor_1_out, or_2_out);
  xor xor_1 (xor_1_out, A[3], B[3]);
  or or_2 (or_2_out, and_3_out, and_4_out);
  xor xor_2 (out_5[3], xor_1_out, or_2_out);
  and and_3 (and_3_out, A[2], B[2]);
  and and_4 (and_4_out, xor_3_out, or_3_out);
  xor xor_3 (xor_3_out, A[2], B[2]);
  xor xor_4 (out_5[2], xor_3_out, or_3_out);
  or or_3 (or_3_out, and_5_out, and_6_out);
  and and_5 (and_5_out, A[1], B[1]);
  and and_6 (and_6_out, xor_5_out, or_4_out);
  xor xor_5 (xor_5_out, A[1], B[1]);
  xor xor_6 (out_5[1], xor_5_out, or_4_out);
  or or_4 (or_4_out, and_7_out, and_8_out);
  and and_7 (and_7_out, A[0], B[0]);
  and and_8 (and_8_out, xor_7_out, in_3);
  xor xor_7 (xor_7_out, A[0], B[0]);
  xor xor_8 (out_5[0], xor_7_out, in_3);
endmodule
