// Logisim project exo2.circ as structural Verilog: 1 circuit, main circuit main
module main (
  input  in_1,
  input  in_2,
  input  in_3,
  input  in_4,
  output out_5
);

  wire transistor_1_out, transistor_4_out, transistor_5_out, transistor_7_out, transistor_8_out;

  Transistor transistor_1 (.in(1'b1), .out(transistor_1_out), .gate(in_1));
  Transistor transistor_2 (.in(transistor_1_out), .out(out_5), .gate(in_3));
  Transistor #(.\type ("n")) transistor_3 (.in(transistor_4_out), .out(out_5), .gate(in_1));
  Transistor #(.\type ("n")) transistor_4 (.in(transistor_8_out), .out(transistor_4_out), .gate(in_3));
  Transistor #(.gate("br")) transistor_5 (.in(1'b1), .out(transistor_5_out), .gate(in_2));
  Transistor #(.gate("br")) transistor_6 (.in(transistor_5_out), .out(out_5), .gate(in_4));
  Transistor #(.\type ("n"), .gate("br")) transistor_7 (.in(out_5), .out(transistor_7_out), .gate(in_2));
  Transistor #(.\type ("n"), .gate("br")) transistor_8 (.in(transistor_7_out), .out(transistor_8_out), .gate(in_4));
  // also tied to GND on the sheet: transistor_8_out

  // Other names for the same wires on the sheet: A = in_1; B = in_2; C = in_3; D = in_4
endmodule
