// Logisim project exercice2.circ as structural Verilog: 1 circuit, main circuit main
module main (
  input  [3:0] A,
  input  [3:0] B,
  output Carry,
  output [3:0] Resultat
);

  wire and_1_out, and_2_out, and_3_out, and_4_out, and_5_out, and_6_out, and_7_out, and_8_out, not_1_out,
       not_2_out, not_3_out, not_4_out, or_2_out, or_3_out, or_4_out, xor_1_out, xor_3_out, xor_5_out,
       xor_7_out;

  or or_1 (Carry, and_1_out, and_2_out);
  and and_1 (and_1_out, A[3], not_1_out);
  and and_2 (and_2_out, xor_1_out, or_2_out);
  not not_1 (not_1_out, B[3]);
  xor xor_1 (xor_1_out, A[3], not_1_out);
  xor xor_2 (Resultat[3], xor_1_out, or_2_out);
  or or_2 (or_2_out, and_3_out, and_4_out);
  and and_3 (and_3_out, A[2], not_2_out);
  and and_4 (and_4_out, xor_3_out, or_3_out);
  not not_2 (not_2_out, B[2]);
  xor xor_3 (xor_3_out, A[2], not_2_out);
  xor xor_4 (Resultat[2], xor_3_out, or_3_out);
  and and_5 (and_5_out, A[1], not_3_out);
  or or_3 (or_3_out, and_5_out, and_6_out);
  and and_6 (and_6_out, xor_5_out, or_4_out);
  not not_3 (not_3_out, B[1]);
  or or_4 (or_4_out, and_7_out, and_8_out);
  xor xor_5 (xor_5_out, A[1], not_3_out);
  xor xor_6 (Resultat[1], xor_5_out, or_4_out);
  and and_7 (and_7_out, A[0], not_4_out);
  and and_8 (and_8_out, xor_7_out, 1'b1);
  xor xor_7 (xor_7_out, A[0], not_4_out);
  not not_4 (not_4_out, B[0]);
  xor xor_8 (Resultat[0], xor_7_out, 1'b1);
endmodule
