// Logisim project exercice4.circ as structural Verilog: 1 circuit, main circuit main
module main (
  input  [3:0] A,
  input  [3:0] B,
  input  [3:0] C,
  input  [3:0] D,
  input  [7:0] in_5,
  output Carry,
  output Overflow,
  output Negative,
  output Zero,
  output [3:0] Resultat
);

  wire and_1_out, and_2_out, and_3_out, and_4_out, and_5_out, and_6_out, and_7_out, and_8_out, and_9_out,
       and_10_out, and_11_out, and_12_out, and_13_out, and_14_out, and_15_out, not_1_out, or_2_out, or_3_out,
       or_4_out, or_6_out, or_7_out, xnor_1_out, xnor_2_out, xnor_3_out, xor_2_out, xor_3_out, xor_5_out,
       xor_6_out, xor_8_out, xor_9_out, xor_11_out, xor_12_out;
  wire [0:0] or_5_out;
  wire [2:0] xor_13_out;
  wire [3:0] multiplexer_1_out, multiplexer_2_out;

  Multiplexer #(.select(2), .width(4), .enable("false")) multiplexer_1 (
    .in0(A), .in1(B), .in2(C), .in3(D), .out(multiplexer_1_out), .sel(in_5[7:6]));
  xor xor_1 (Overflow, Carry, or_2_out);
  nor nor_1 (Zero, Negative, xor_13_out[2], xor_13_out[1], xor_13_out[0]);
  Multiplexer #(.select(2), .width(4), .enable("false")) multiplexer_2 (
    .in0(A), .in1(B), .in2(C), .in3(D), .out(multiplexer_2_out), .sel(in_5[5:4]));
  or or_1 (Carry, and_1_out, and_2_out);
  Multiplexer #(.width(4), .enable("false")) multiplexer_3 (
    .in0({Negative, xor_13_out}), .in1({3'b000, or_5_out[0]}), .out(Resultat), .sel(in_5[1]));
  and and_1 (and_1_out, multiplexer_2_out[3], xor_2_out);
  and and_2 (and_2_out, xor_3_out, or_2_out);
  xor xor_2 (xor_2_out, ~multiplexer_1_out[3], in_5[0]);  // XOR_Gate
  xor xor_3 (xor_3_out, multiplexer_2_out[3], xor_2_out);
  xor xor_4 (Negative, xor_3_out, or_2_out);
  or or_2 (or_2_out, and_3_out, and_4_out);
  and and_3 (and_3_out, multiplexer_2_out[2], xor_5_out);
  and and_4 (and_4_out, xor_6_out, or_3_out);
  xor xor_5 (xor_5_out, ~multiplexer_1_out[2], in_5[0]);  // XOR_Gate
  or or_3 (or_3_out, and_5_out, and_6_out);
  xor xor_6 (xor_6_out, multiplexer_2_out[2], xor_5_out);
  xor xor_7 (xor_13_out[2], xor_6_out, or_3_out);
  and and_5 (and_5_out, multiplexer_2_out[1], xor_9_out);
  and and_6 (and_6_out, xor_8_out, or_4_out);
  xor xor_8 (xor_8_out, multiplexer_2_out[1], xor_9_out);
  xor xor_9 (xor_9_out, ~multiplexer_1_out[1], in_5[0]);  // XOR_Gate
  or or_4 (or_4_out, and_7_out, and_8_out);
  xor xor_10 (xor_13_out[1], xor_8_out, or_4_out);
  and and_7 (and_7_out, multiplexer_2_out[0], xor_11_out);
  and and_8 (and_8_out, xor_12_out, not_1_out);
  xor xor_11 (xor_11_out, ~multiplexer_1_out[0], in_5[0]);  // XOR_Gate
  xor xor_12 (xor_12_out, multiplexer_2_out[0], xor_11_out);
  xor xor_13 (xor_13_out[0], xor_12_out, not_1_out);
  not not_1 (not_1_out, in_5[0]);
  and and_9 (and_9_out, ~multiplexer_2_out[3], multiplexer_1_out[3]);  // AND_Gate
  or or_5 (or_5_out[0], and_9_out, and_10_out);
  xnor xnor_1 (xnor_1_out, multiplexer_2_out[3], multiplexer_1_out[3]);
  and and_10 (and_10_out, xnor_1_out, or_6_out);
  and and_11 (and_11_out, ~multiplexer_2_out[2], multiplexer_1_out[2]);  // AND_Gate
  or or_6 (or_6_out, and_11_out, and_12_out);
  xnor xnor_2 (xnor_2_out, multiplexer_2_out[2], multiplexer_1_out[2]);
  and and_12 (and_12_out, xnor_2_out, or_7_out);
  and and_13 (and_13_out, ~multiplexer_2_out[1], multiplexer_1_out[1]);  // AND_Gate
  or or_7 (or_7_out, and_13_out, and_14_out);
  xnor xnor_3 (xnor_3_out, multiplexer_2_out[1], multiplexer_2_out[2]);
  and and_14 (and_14_out, xnor_3_out, and_15_out);
  and and_15 (and_15_out, ~multiplexer_2_out[0], multiplexer_1_out[0]);  // AND_Gate
endmodule
